# Fritzing sketch experimental (saved by Fritzing 0.9.9b)
breadboards: 2

parts:
  Part1 = Arduino Nano (Rev3.0)
  R1 = Resistor [tolerance=±5% power=0.25 resistance=1k package=THT]
  LED1 = LED - 5mm [color="Red (633nm)" current=0.030 package="5 mm [THT]"]
  U2 = SN74LS20N [package="DIP14 [THT]"]
  S1 = Toggle Switch [package=THT]
  S2 = Toggle Switch [package=THT]
  Keypad4x1 = Keypad Membran 4x4
  U3 = 74HC595 SMD [package="SO16 [SMD]"]  # not connected
  LCD1 = LCD screen  # not connected
  R2 = Trimmer Potentiometer [maximum_resistance=10kΩ package=THT]  # not connected
  S3 = Momentary Switch 6mm 2pin
  S4 = Momentary Switch 6mm 2pin
  Part2 = Arduino Nano Every  # not connected
  M1 = Arduino Nano 33 IOT-tht  # not connected
  Q1 = TRANSISTOR_NPN [package=to-92]  # not connected
  U4 = SN74LS20N [package="DIP14 [THT]"]
  S5 = Pushbutton [package="[THT]"]
  S6 = Pushbutton [package="[THT]"]

nets:
  GND: Part1.GND, LED1.cathode, U2.GND, S1.COM, S2.COM, S3.2, S4.2
  N1: Part1.D2, U2.1Y
  N2: Part1.D3, U2.2Y
  N3: Part1.D4, Keypad4x1.Pin1
  N4: Part1.D5, Keypad4x1.Pin2
  N5: Part1.D6, Keypad4x1.Pin3
  N6: Part1.D7, Keypad4x1.Pin4
  N7: Part1.D8, U2.1D, S4.1
  N8: Part1.D9, U2.1A, S3.1
  N9: Part1.D12/MISO, R1.Pin_0
  5V: Part1.5V, U2.1B, U2.1C, U2.VCC
  N10: Part1.A5, S2.L1
  N11: Part1.A4, S1.L1
  N12: Part1.A3, U2.2A, Keypad4x1.Pin8
  N13: Part1.A2, U2.2B, Keypad4x1.Pin7
  N14: Part1.A1, U2.2C, Keypad4x1.Pin6
  N15: Part1.A0, U2.2D, Keypad4x1.Pin5
  N16: R1.Pin_1, LED1.anode
  N17: U4.1B, S6.Pin_1, S6.Pin_2
  N18: U4.NC#2, S5.Pin_3, S5.Pin_4
  N19: U4.1D, S5.Pin_1, S5.Pin_2
  N20: S6.Pin_3, S6.Pin_4

custom parts:
  Keypad Membran 4x4: Membrane Keypad 4x4 Matrix
  Momentary Switch 6mm 2pin: Momentary Switch 6mm 2 pin Button commonly used for reset or general input.
  Arduino Nano Every: The Nano Every is Arduino’s 5V compatible board in the smallest available form factor: 45x18mm! The Arduino Nano is the preferred board for many projects requiring a small and easy to use microcontroller board. The small footprint and low price, make the Nano Every particularly suited for wearable inventions, low cost robotics, electronic musical instruments, and general use to control smaller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
  Arduino Nano 33 IOT-tht: The Arduino Nano 33 IoT is the easiest and cheapest point of entry to enhance existing devices (and creating new ones) to be part of the IoT and designing pico-network applications. Whether you are looking at building a sensor network connected to your office or home router, or if you want to create a BLE device sending data to a cellphone, the Nano 33 IoT is your one-stop-solution for many of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
